// Logisim project s-mips.circ as structural Verilog: 9 circuits, main circuit S-MIPS Board
module S_MIPS_Board (
  input  DESHABILITAR_DISPATCHER,
  output halt
);

  wire button_1_out, CLK, CS, d_ff_1_q, LCLR, LoadRAM, LoadRAMOn, LW, R_R_W, R_W, ram_dispatcher_1_finished,
       RCS, Reset_out, RST, TTY_EN;
  wire [2:0] KDB;
  wire [3:0] LMask, Mask, ram_1_read_time, ram_1_write_time, RMask;
  wire [6:0] KDB_DATA, TTY_DATA;
  wire [15:0] Addr, LAddr, RAddr;
  wire [31:0] I0, I1, I2, I3, LData, ram_1_data_out_0, ram_1_data_out_1, ram_1_data_out_2, ram_1_data_out_3,
       RI0, RI1, RI2, RI3;

  TTY #(.rows(25), .cols(80)) tty_1 (.data(TTY_DATA), .clk(CLK), .we(TTY_EN), .clr(RST));
  not not_1 (LoadRAMOn, ram_dispatcher_1_finished);
  RAM_Dispatcher ram_dispatcher_1 (
    .WriteTime(ram_1_write_time), .Clock(CLK), .Data(LData), .Address(LAddr), .Mask(LMask),
    .Finished(ram_dispatcher_1_finished), .Write(LW), .CLR(LCLR));
  Keyboard #(.buflen(64)) keyboard_1 (.clk(CLK), .re(KDB[0]), .avail(KDB[2]), .data(KDB_DATA));  // open: clr
  RAM ram_1 (
    .Address(RAddr), .Data_Out_0(ram_1_data_out_0), .Data_Out_1(ram_1_data_out_1),
    .Data_Out_2(ram_1_data_out_2), .Data_Out_3(ram_1_data_out_3), .Data_In_0(RI0), .Data_In_1(RI1),
    .Data_In_2(RI2), .Data_In_3(RI3), .Mask(RMask), .nRead_Write(R_R_W), .Chip_Select(RCS),
    .Read_Time(ram_1_read_time), .Reset(button_1_out), .Write_Time(ram_1_write_time));
  Button button_1 (.out(button_1_out));
  D_Flip_Flop d_ff_1 (.clk(CLK), .D(1'b1), .Q(d_ff_1_q), .reset(Reset_out));  // open: Qn, preset, en
  Button Reset (.out(Reset_out));
  S_MIPS s_mips_1 (
    .Kbd_Enable(KDB[0]), .Address(Addr), .Kbd_Clear(KDB[1]), .Kbd_Available(KDB[2]), .RAM_In_0(I0),
    .Kbd_ASCII_Data(KDB_DATA), .RAM_In_1(I1), .TTY_Enable(TTY_EN), .RAM_In_2(I2), .RAM_In_3(I3),
    .TTY_ASCII_Data(TTY_DATA), .Reset(RST), .RAM_Out_0(ram_1_data_out_0), .Clock(CLK),
    .RAM_Out_1(ram_1_data_out_1), .Stop(halt), .RAM_Out_2(ram_1_data_out_2), .RAM_Out_3(ram_1_data_out_3),
    .Mask(Mask), .Read_Time(ram_1_read_time), .Write_Time(ram_1_write_time), .nRead_Write(R_W),
    .Chip_Select(CS));
  D_Flip_Flop d_ff_2 (.clk(CLK), .D(d_ff_1_q), .Qn(LCLR), .reset(Reset_out));  // open: Q, preset, en
  or or_1 (RST, LCLR, LoadRAM);
  Clock clock_1 (.out(CLK));
  Multiplexer #(.width(32), .enable("false")) multiplexer_1 (.in0(I0), .in1(LData), .out(RI0), .sel(LoadRAM));
  Multiplexer #(.width(32), .enable("false")) multiplexer_2 (.in0(I1), .in1(LData), .out(RI1), .sel(LoadRAM));
  Multiplexer #(.width(32), .enable("false")) multiplexer_3 (.in0(I2), .in1(LData), .out(RI2), .sel(LoadRAM));
  Multiplexer #(.width(32), .enable("false")) multiplexer_4 (.in0(I3), .in1(LData), .out(RI3), .sel(LoadRAM));
  and and_1 (LoadRAM, ~DESHABILITAR_DISPATCHER, LoadRAMOn);  // AND_Gate
  Multiplexer #(.width(16), .enable("false")) multiplexer_5 (.in0(Addr), .in1(LAddr), .out(RAddr), .sel(LoadRAM));
  Multiplexer #(.width(4), .enable("false")) multiplexer_6 (.in0(Mask), .in1(LMask), .out(RMask), .sel(LoadRAM));
  Multiplexer #(.enable("false")) multiplexer_7 (.in0(CS), .in1(LW), .out(RCS), .sel(LoadRAM));
  Multiplexer #(.enable("false")) multiplexer_8 (.in0(R_W), .in1(LW), .out(R_R_W), .sel(LoadRAM));

  // Notes on the sheet:
  //   NO MODIFICAR
  //   Keyboard
endmodule

module RAM (
  input  [15:0] Address,
  input  [31:0] Data_In_0,
  input  [31:0] Data_In_1,
  input  [31:0] Data_In_2,
  input  [31:0] Data_In_3,
  input  [3:0] Mask,
  input  nRead_Write,
  input  Chip_Select,
  input  Reset,
  output [31:0] Data_Out_0,
  output [31:0] Data_Out_1,
  output [31:0] Data_Out_2,
  output [31:0] Data_Out_3,
  output [3:0] Read_Time,
  output [3:0] Write_Time
);

  wire and_2_out, and_3_out, and_4_out, and_5_out, and_6_out, and_7_out, and_8_out, and_9_out, Changed, CLK,
       comparator_2_eq, comparator_3_eq, comparator_4_eq, comparator_5_eq, comparator_6_eq, Count,
       demultiplexer_3_out0, Idle, Idle_q, Load, Load0, Load1, nand_1_out, or_1_out, or_2_out, or_3_out,
       or_4_out, or_5_out, or_6_out, or_7_out, or_8_out, or_9_out, or_10_out, Proc_q, Update_Mem, Zero_Time;
  wire [3:0] counter_1_q, multiplexer_1_out, subtractor_1_out;
  wire [31:0] register_1_q, register_2_q, register_3_q, register_4_q, register_5_q;

  // Probe on 4'b0011
  // Probe on 4'b0010
  Multiplexer #(.width(4), .enable("false")) multiplexer_1 (
    .in0(4'b0011), .in1(4'b0010), .out(multiplexer_1_out), .sel(nRead_Write));
  or or_1 (or_1_out, Idle, Update_Mem);
  or or_2 (or_2_out, ~Chip_Select, Reset);  // OR_Gate
  Subtractor #(.width(4)) subtractor_1 (.a(multiplexer_1_out), .b(4'b0010), .out(subtractor_1_out));  // open: bin, bout
  Demultiplexer #(.enable("false")) demultiplexer_1 (.out0(Idle), .out1(Load0), .in(Idle_q), .sel(Changed));
  D_Flip_Flop u_Idle (.clk(CLK), .D(or_1_out), .Q(Idle_q), .preset(or_2_out));  // open: Qn, en, reset
  // Probe on counter_1_q
  Counter #(.width(4), .max('hf)) counter_1 (
    .load(Load), .D(subtractor_1_out), .count(Count), .Q(counter_1_q), .clk(CLK), .clr(or_3_out));  // open: carry
  or or_3 (or_3_out, ~Chip_Select, Reset);  // OR_Gate
  Comparator #(.width(4), .mode("unsigned")) comparator_1 (
    .a(4'b0000), .b(counter_1_q), .eq(Zero_Time));  // open: gt, lt
  or or_4 (or_4_out, Count, Load0, Load1);
  Register #(.width(32)) register_1 (.D(Data_In_0), .en(Chip_Select), .Q(register_1_q), .clk(CLK), .clr(or_5_out));
  or or_5 (or_5_out, ~Chip_Select, Reset);  // OR_Gate
  Register #(.width(32)) register_2 (.D(Data_In_1), .en(Chip_Select), .Q(register_2_q), .clk(CLK), .clr(or_6_out));
  or or_6 (or_6_out, ~Chip_Select, Reset);  // OR_Gate
  Register #(.width(32)) register_3 (.D(Data_In_2), .en(Chip_Select), .Q(register_3_q), .clk(CLK), .clr(or_7_out));
  or or_7 (or_7_out, ~Chip_Select, Reset);  // OR_Gate
  Register #(.width(32)) register_4 (.D(Data_In_3), .en(Chip_Select), .Q(register_4_q), .clk(CLK), .clr(or_8_out));
  or or_8 (or_8_out, ~Chip_Select, Reset);  // OR_Gate
  Register #(.width(32)) register_5 (
    .D({{11{1'b1}}, nRead_Write, Mask, Address}), .en(Chip_Select), .Q(register_5_q), .clk(CLK),
    .clr(or_9_out));
  or or_9 (or_9_out, ~Chip_Select, Reset);  // OR_Gate
  D_Flip_Flop Proc (.clk(CLK), .D(or_4_out), .Q(Proc_q), .reset(or_10_out));  // open: Qn, preset, en
  or or_10 (or_10_out, ~Chip_Select, Reset);  // OR_Gate
  Demultiplexer #(.enable("false")) demultiplexer_2 (
    .out0(Count), .out1(Update_Mem), .in(demultiplexer_3_out0), .sel(Zero_Time));
  Demultiplexer #(.enable("false")) demultiplexer_3 (
    .out0(demultiplexer_3_out0), .out1(Load1), .in(Proc_q), .sel(Changed));
  Clock clock_1 (.out(CLK));
  Comparator #(.width(32)) comparator_2 (.a(register_1_q), .b(Data_In_0), .eq(comparator_2_eq));  // open: gt, lt
  Comparator #(.width(32)) comparator_3 (.a(register_2_q), .b(Data_In_1), .eq(comparator_3_eq));  // open: gt, lt
  Comparator #(.width(32)) comparator_4 (.a(register_3_q), .b(Data_In_2), .eq(comparator_4_eq));  // open: gt, lt
  Comparator #(.width(32)) comparator_5 (.a(register_4_q), .b(Data_In_3), .eq(comparator_5_eq));  // open: gt, lt
  Comparator #(.width(32)) comparator_6 (
    .a(register_5_q), .b({{11{1'b1}}, nRead_Write, Mask, Address}), .eq(comparator_6_eq));  // open: gt, lt
  nand nand_1 (nand_1_out, comparator_6_eq, comparator_2_eq, comparator_3_eq, comparator_4_eq, comparator_5_eq);
  and and_1 (Changed, nand_1_out, Chip_Select);
  or or_11 (Load, Count, Load1, Load0);
  and and_2 (and_2_out, Mask[0], Update_Mem, nRead_Write);
  and and_3 (and_3_out, Mask[1], Update_Mem, nRead_Write);
  and and_4 (and_4_out, Mask[2], Update_Mem, nRead_Write);
  and and_5 (and_5_out, Mask[3], Update_Mem, nRead_Write);
  RAM_part #(.addrWidth(16), .dataWidth(32), .bus("separate")) ram_1 (
    .addr(Address), .din(Data_In_0), .data(Data_Out_0), .str(and_2_out), .sel(Chip_Select), .clk(CLK),
    .ld(and_6_out), .clr(Reset));
  and and_6 (and_6_out, ~nRead_Write, Idle);  // AND_Gate
  RAM_part #(.addrWidth(16), .dataWidth(32), .bus("separate")) ram_2 (
    .addr(Address), .din(Data_In_1), .data(Data_Out_1), .str(and_3_out), .sel(Chip_Select), .clk(CLK),
    .ld(and_7_out), .clr(Reset));
  and and_7 (and_7_out, ~nRead_Write, Idle);  // AND_Gate
  RAM_part #(.addrWidth(16), .dataWidth(32), .bus("separate")) ram_3 (
    .addr(Address), .din(Data_In_2), .data(Data_Out_2), .str(and_4_out), .sel(Chip_Select), .clk(CLK),
    .ld(and_8_out), .clr(Reset));
  and and_8 (and_8_out, ~nRead_Write, Idle);  // AND_Gate
  RAM_part #(.addrWidth(16), .dataWidth(32), .bus("separate")) ram_4 (
    .addr(Address), .din(Data_In_3), .data(Data_Out_3), .str(and_5_out), .sel(Chip_Select), .clk(CLK),
    .ld(and_9_out), .clr(Reset));
  and and_9 (and_9_out, ~nRead_Write, Idle);  // AND_Gate

  assign Read_Time = 4'b0011;
  assign Write_Time = 4'b0010;

  // Other names for the same wires on the sheet: M0 = Mask[0]; M1 = Mask[1]; M2 = Mask[2]; M3 = Mask[3];
  //   RW = nRead_Write; CLR = Reset; CS = Chip_Select; Load2 = Count

  // Notes on the sheet:
  //   NO MODIFICAR
  //   excepto quizás los valores RT y WT
  //   BANK0
  //   BANK1
  //   BANK2
  //   BANK3
endmodule

module S_MIPS (
  input  Kbd_Available,
  input  [6:0] Kbd_ASCII_Data,
  input  [31:0] RAM_Out_0,
  input  [31:0] RAM_Out_1,
  input  Reset,
  input  [31:0] RAM_Out_2,
  input  Clock,
  input  [31:0] RAM_Out_3,
  input  [3:0] Read_Time,
  input  [3:0] Write_Time,
  output Kbd_Enable,
  output [15:0] Address,
  output Kbd_Clear,
  output TTY_Enable,
  output [6:0] TTY_ASCII_Data,
  output Stop,
  output [31:0] RAM_In_0,
  output [31:0] RAM_In_1,
  output [31:0] RAM_In_2,
  output [31:0] RAM_In_3,
  output [3:0] Mask,
  output nRead_Write,
  output Chip_Select
);


  // Other names for the same wires on the sheet: CLK = Clock; CLR = Reset; CS = Chip_Select;
  //   KBD_AVAIL = Kbd_Available; KBD_CLR = Kbd_Clear; KBD_DATA[6:0] = Kbd_ASCII_Data; RAM_A[15:0] = Address;
  //   RAM_INPUT_0[31:0] = RAM_In_0; RAM_INPUT_1[31:0] = RAM_In_1; RAM_INPUT_2[31:0] = RAM_In_2;
  //   RAM_INPUT_3[31:0] = RAM_In_3; RAM_MASK[3:0] = Mask; RAM_OUTPUT_0[31:0] = RAM_Out_0;
  //   RAM_OUTPUT_1[31:0] = RAM_Out_1; RAM_OUTPUT_2[31:0] = RAM_Out_2; RAM_OUTPUT_3[31:0] = RAM_Out_3;
  //   RW = nRead_Write; TTY_DATA[6:0] = TTY_ASCII_Data

  // Notes on the sheet:
  //   RAM ADDRESS
  //   DATA FROM RAM
  //   DATA TO RAM
  //   DATA WRITE MASK
  //   RAM TIMING
  //   RAM CONTROL
  //   KEYBOARD
  //   TTY
  //   SEQUENCING
endmodule

module RAM_Dispatcher (
  input  [3:0] WriteTime,
  input  Clock,
  input  CLR,
  output [31:0] Data,
  output [15:0] Address,
  output [3:0] Mask,
  output Finished,
  output Write
);

  wire demultiplexer_2_out1, demultiplexer_3_out1, End, IDLE_q, IncAddr, Load, or_1_out, or_2_out, While_q,
       WriteEnd;
  wire [3:0] counter_1_q;
  wire [31:0] CurrentAddress_q;

  Counter #(.width(32), .max('hffffffff)) CurrentAddress (
    .count(IncAddr), .Q({CurrentAddress_q[31:18], Address, CurrentAddress_q[1:0]}), .clk(Clock), .clr(CLR));  // open: load, D, carry
  or or_1 (or_1_out, IncAddr, demultiplexer_3_out1, Finished);
  D_Flip_Flop IDLE (.clk(Clock), .D(or_1_out), .Q(IDLE_q), .preset(CLR));  // open: Qn, en, reset
  Demultiplexer #(.enable("false")) demultiplexer_1 (.out0(Load), .out1(Finished), .in(IDLE_q), .sel(End));
  D_Flip_Flop While (.clk(Clock), .D(or_2_out), .Q(While_q), .reset(CLR));  // open: Qn, preset, en
  or or_2 (or_2_out, Write, Load);
  RAM_part #(.addrWidth(18), .dataWidth(32)) ram_1 (
    .addr({Address, CurrentAddress_q[1:0]}), .data(Data), .clk(Clock));  // open: sel, ld, clr
  Demultiplexer #(.enable("false")) demultiplexer_2 (
    .out0(Write), .out1(demultiplexer_2_out1), .in(While_q), .sel(WriteEnd));
  Decoder #(.select(2)) decoder_1 (
    .out0(Mask[0]), .out1(Mask[1]), .out2(Mask[2]), .out3(Mask[3]), .sel(CurrentAddress_q[1:0]));  // open: en
  Demultiplexer #(.enable("false")) demultiplexer_3 (
    .out0(IncAddr), .out1(demultiplexer_3_out1), .in(demultiplexer_2_out1), .sel(End));
  Counter #(.width(4), .max('hf)) counter_1 (
    .load(Load), .D(WriteTime), .count(Write), .Q(counter_1_q), .clk(Clock));  // open: carry, clr
  Comparator #(.width(32)) comparator_1 (.a(Data), .b({32{1'b1}}), .eq(End));  // open: gt, lt
  Comparator #(.width(4)) comparator_2 (.a(4'b0000), .b(counter_1_q), .eq(WriteEnd));  // open: gt, lt

  // Other names for the same wires on the sheet: CLK = Clock; Count = Write; WT[3:0] = WriteTime
endmodule

module Register_File (
  input  Write_1___Read_0,
  input  Reset,
  input  Clock,
  input  [31:0] in_4,
  input  [4:0] S__Output_A,
  input  [4:0] S__Output_B,
  input  [4:0] S__Register_to_Write,
  output [31:0] Output_A,
  output [31:0] Output_B
);

  wire R0, R1, R2, R3, R4, R5, R6, R7, R8, R9, R10, R11, R12, R13, R14, R15, R16, R17, R18, R19, R20, R21,
       R22, R23, R24, R25, R26, R27, R28, R29, R30, R31;
  wire [31:0] OutP_0, OutP_1, OutP_2, OutP_3, OutP_4, OutP_5, OutP_6, OutP_7, OutP_8, OutP_9, OutP_10,
       OutP_11, OutP_12, OutP_13, OutP_14, OutP_15, OutP_16, OutP_17, OutP_18, OutP_19, OutP_20, OutP_21,
       OutP_22, OutP_23, OutP_24, OutP_25, OutP_26, OutP_27, OutP_28, OutP_29, OutP_30, OutP_31;

  Multiplexer #(.select(5), .width(32), .enable("false")) multiplexer_1 (
    .in0(OutP_0), .in1(OutP_1), .in2(OutP_2), .in3(OutP_3), .in4(OutP_4), .in5(OutP_5), .in6(OutP_6),
    .in7(OutP_7), .in8(OutP_8), .in9(OutP_9), .in10(OutP_10), .in11(OutP_11), .in12(OutP_12), .in13(OutP_13),
    .in14(OutP_14), .in15(OutP_15), .in16(OutP_16), .in17(OutP_17), .in18(OutP_18), .in19(OutP_19),
    .in20(OutP_20), .in21(OutP_21), .in22(OutP_22), .in23(OutP_23), .in24(OutP_24), .in25(OutP_25),
    .in26(OutP_26), .in27(OutP_27), .in28(OutP_28), .in29(OutP_29), .in30(OutP_30), .in31(OutP_31),
    .out(Output_A), .sel(S__Output_A));
  Demultiplexer #(.select(5), .enable("false")) demultiplexer_1 (
    .out0(R0), .out1(R1), .out2(R2), .out3(R3), .out4(R4), .out5(R5), .out6(R6), .out7(R7), .out8(R8),
    .out9(R9), .out10(R10), .out11(R11), .out12(R12), .out13(R13), .out14(R14), .out15(R15), .out16(R16),
    .out17(R17), .out18(R18), .out19(R19), .out20(R20), .out21(R21), .out22(R22), .out23(R23), .out24(R24),
    .out25(R25), .out26(R26), .out27(R27), .out28(R28), .out29(R29), .out30(R30), .out31(R31),
    .in(Write_1___Read_0), .sel(S__Register_to_Write));
  Multiplexer #(.select(5), .width(32), .enable("false")) multiplexer_2 (
    .in0(OutP_0), .in1(OutP_1), .in2(OutP_2), .in3(OutP_3), .in4(OutP_4), .in5(OutP_5), .in6(OutP_6),
    .in7(OutP_7), .in8(OutP_8), .in9(OutP_9), .in10(OutP_10), .in11(OutP_11), .in12(OutP_12), .in13(OutP_13),
    .in14(OutP_14), .in15(OutP_15), .in16(OutP_16), .in17(OutP_17), .in18(OutP_18), .in19(OutP_19),
    .in20(OutP_20), .in21(OutP_21), .in22(OutP_22), .in23(OutP_23), .in24(OutP_24), .in25(OutP_25),
    .in26(OutP_26), .in27(OutP_27), .in28(OutP_28), .in29(OutP_29), .in30(OutP_30), .in31(OutP_31),
    .out(Output_B), .sel(S__Output_B));
  Register #(.width(32)) u_R0 (.D({32{1'b0}}), .en(R0), .Q(OutP_0), .clk(Clock), .clr(Reset));
  Register #(.width(32)) u_R5 (.D(in_4), .en(R5), .Q(OutP_5), .clk(Clock), .clr(Reset));
  Register #(.width(32)) u_R10 (.D(in_4), .en(R10), .Q(OutP_10), .clk(Clock), .clr(Reset));
  Register #(.width(32)) u_R15 (.D(in_4), .en(R15), .Q(OutP_15), .clk(Clock), .clr(Reset));
  Register #(.width(32)) u_R20 (.D(in_4), .en(R20), .Q(OutP_20), .clk(Clock), .clr(Reset));
  Register #(.width(32)) u_R25 (.D(in_4), .en(R25), .Q(OutP_25), .clk(Clock), .clr(Reset));
  Register #(.width(32)) u_R30 (.D(in_4), .en(R30), .Q(OutP_30), .clk(Clock), .clr(Reset));
  Register #(.width(32)) u_R1 (.D(in_4), .en(R1), .Q(OutP_1), .clk(Clock), .clr(Reset));
  Register #(.width(32)) u_R6 (.D(in_4), .en(R6), .Q(OutP_6), .clk(Clock), .clr(Reset));
  Register #(.width(32)) u_R11 (.D(in_4), .en(R11), .Q(OutP_11), .clk(Clock), .clr(Reset));
  Register #(.width(32)) u_R16 (.D(in_4), .en(R16), .Q(OutP_16), .clk(Clock), .clr(Reset));
  Register #(.width(32)) u_R21 (.D(in_4), .en(R21), .Q(OutP_21), .clk(Clock), .clr(Reset));
  Register #(.width(32)) u_R26 (.D(in_4), .en(R26), .Q(OutP_26), .clk(Clock), .clr(Reset));
  Register #(.width(32)) R31___Stack_Pointer (.D(in_4), .en(R31), .Q(OutP_31), .clk(Clock), .clr(Reset));
  Register #(.width(32)) u_R2 (.D(in_4), .en(R2), .Q(OutP_2), .clk(Clock), .clr(Reset));
  Register #(.width(32)) u_R7 (.D(in_4), .en(R7), .Q(OutP_7), .clk(Clock), .clr(Reset));
  Register #(.width(32)) u_R12 (.D(in_4), .en(R12), .Q(OutP_12), .clk(Clock), .clr(Reset));
  Register #(.width(32)) u_R17 (.D(in_4), .en(R17), .Q(OutP_17), .clk(Clock), .clr(Reset));
  Register #(.width(32)) u_R22 (.D(in_4), .en(R22), .Q(OutP_22), .clk(Clock), .clr(Reset));
  Register #(.width(32)) u_R27 (.D(in_4), .en(R27), .Q(OutP_27), .clk(Clock), .clr(Reset));
  Register #(.width(32)) u_R3 (.D(in_4), .en(R3), .Q(OutP_3), .clk(Clock), .clr(Reset));
  Register #(.width(32)) u_R8 (.D(in_4), .en(R8), .Q(OutP_8), .clk(Clock), .clr(Reset));
  Register #(.width(32)) u_R13 (.D(in_4), .en(R13), .Q(OutP_13), .clk(Clock), .clr(Reset));
  Register #(.width(32)) u_R18 (.D(in_4), .en(R18), .Q(OutP_18), .clk(Clock), .clr(Reset));
  Register #(.width(32)) u_R23 (.D(in_4), .en(R23), .Q(OutP_23), .clk(Clock), .clr(Reset));
  Register #(.width(32)) u_R28 (.D(in_4), .en(R28), .Q(OutP_28), .clk(Clock), .clr(Reset));
  Register #(.width(32)) u_R4 (.D(in_4), .en(R4), .Q(OutP_4), .clk(Clock), .clr(Reset));
  Register #(.width(32)) u_R9 (.D(in_4), .en(R9), .Q(OutP_9), .clk(Clock), .clr(Reset));
  Register #(.width(32)) u_R14 (.D(in_4), .en(R14), .Q(OutP_14), .clk(Clock), .clr(Reset));
  Register #(.width(32)) u_R19 (.D(in_4), .en(R19), .Q(OutP_19), .clk(Clock), .clr(Reset));
  Register #(.width(32)) u_R24 (.D(in_4), .en(R24), .Q(OutP_24), .clk(Clock), .clr(Reset));
  Register #(.width(32)) u_R29 (.D(in_4), .en(R29), .Q(OutP_29), .clk(Clock), .clr(Reset));

  // Other names for the same wires on the sheet: Clk = Clock; Input[31:0] = in_4; R = Reset; S_A[4:0] = S__Output_A;
  //   S_B[4:0] = S__Output_B; S_R_W[4:0] = S__Register_to_Write; W_R = Write_1___Read_0

  // Notes on the sheet:
  //   Selector of Register to Write
  //   Registers
endmodule

module ALU (
  input  [31:0] Num_A,
  input  [31:0] Num_B,
  input  [3:0] S__Operation,
  output [31:0] Outp__A_Op_B,
  output [31:0] Aux__Outp__A_Op_B
);

  wire comparator_1_lt, comparator_2_lt;
  wire [31:0] Add, And, Div, Div_Rest, Divu, Divu_Rest, Mult_H0, Mult_L0, Mulu_H0, Mulu_L0, Nor, Or, STL,
       STLU, Sub, Xor;

  Adder #(.width(32)) adder_1 (.a(Num_A), .b(Num_B), .out(Add));  // open: cin, cout
  Subtractor #(.width(32)) subtractor_1 (.a(Num_A), .b(Num_B), .out(Sub));  // open: bin, bout
  Multiplier #(.width(32)) multiplier_1 (.a(Num_A), .b(Num_B), .out(Mult_L0), .cout(Mult_H0));  // open: cin
  Unsigned_Mult unsigned_mult_1 (.in_1(Num_B), .in_2(Num_A), .Outp__Low(Mulu_L0), .Outp__High(Mulu_H0));
  Signed_Div signed_div_1 (.in_1(Num_A), .in_2(Num_B), .Output_L(Div), .Output_H(Div_Rest));
  Divider #(.width(32)) divider_1 (.a(Num_A), .b(Num_B), .out(Divu), .upper({32{1'b0}}), .rem(Divu_Rest));
  assign And = Num_A & Num_B;  // AND_Gate And, 32 bits wide
  assign Or = Num_A | Num_B;  // OR_Gate Or, 32 bits wide
  assign Nor = ~(Num_A | Num_B);  // NOR_Gate Nor, 32 bits wide
  assign Xor = Num_A ^ Num_B;  // XOR_Gate Xor, 32 bits wide
  Comparator #(.width(32), .mode("unsigned")) comparator_1 (
    .a(Num_A), .b(Num_B), .lt(comparator_1_lt));  // open: gt, eq
  Comparator #(.width(32)) comparator_2 (.a(Num_A), .b(Num_B), .lt(comparator_2_lt));  // open: gt, eq
  assign STL = {{31{1'b0}}, comparator_1_lt};  // Bit_Extender bit_extender_1
  assign STLU = {{31{1'b0}}, comparator_2_lt};  // Bit_Extender bit_extender_2
  Multiplexer #(.select(4), .width(32), .enable("false")) multiplexer_1 (
    .in0(Add), .in1(Sub), .in2(Mult_L0), .in3(Mulu_L0), .in4(Div), .in5(Divu), .in6(And), .in7(Or),
    .in8(Nor), .in9(Xor), .in10(STL), .in11(STLU), .in12({32{1'b0}}), .in13({32{1'b0}}), .in14({32{1'b0}}),
    .in15({32{1'b0}}), .out(Outp__A_Op_B), .sel(S__Operation));
  Multiplexer #(.select(4), .width(32), .enable("false")) multiplexer_2 (
    .in0({32{1'b0}}), .in1({32{1'b0}}), .in2(Mult_H0), .in3(Mulu_H0), .in4(Div_Rest), .in5(Divu_Rest),
    .in6({32{1'b0}}), .in7({32{1'b0}}), .in8({32{1'b0}}), .in9({32{1'b0}}), .in10({32{1'b0}}),
    .in11({32{1'b0}}), .in12({32{1'b0}}), .in13({32{1'b0}}), .in14({32{1'b0}}), .in15({32{1'b0}}),
    .out(Aux__Outp__A_Op_B), .sel(S__Operation));

  // Other names for the same wires on the sheet: A[31:0] = Num_A; B[31:0] = Num_B; S__Op[3:0] = S__Operation

  // Notes on the sheet:
  //   STL
  //   STLU
endmodule

module Unsigned_Mult (
  input  [31:0] in_1,
  input  [31:0] in_2,
  output [31:0] Outp__Low,
  output [31:0] Outp__High
);

  wire adder_1_cout, adder_3_cout;
  wire [31:0] a__inferior, a__superior, adder_1_out, adder_2_out, b__inferior, b__superior, inferior,
       inferior_t, superior, superior_1, superior_2;
  wire [31:16] inferior_1, inferior_2, multiplier_1_out, multiplier_2_out;

  assign a__inferior = {{16{1'b0}}, in_1[15:0]};  // Bit_Extender bit_extender_1
  assign a__superior = {{16{1'b0}}, in_1[31:16]};  // Bit_Extender bit_extender_2
  Multiplier #(.width(32)) multiplier_1 (
    .a(a__superior), .b(b__inferior), .out({multiplier_1_out, inferior_1}));  // open: cin, cout
  Multiplier #(.width(32)) multiplier_2 (
    .a(a__inferior), .b(b__superior), .out({multiplier_2_out, inferior_2}));  // open: cin, cout
  assign b__inferior = {{16{1'b0}}, in_2[15:0]};  // Bit_Extender bit_extender_3
  assign b__superior = {{16{1'b0}}, in_2[31:16]};  // Bit_Extender bit_extender_4
  assign superior_1 = {{16{1'b0}}, multiplier_1_out};  // Bit_Extender bit_extender_5
  assign superior_2 = {{16{1'b0}}, multiplier_2_out};  // Bit_Extender bit_extender_6
  Multiplier #(.width(32)) multiplier_3 (.a(a__superior), .b(b__superior), .out(superior));  // open: cin, cout
  Multiplier #(.width(32)) multiplier_4 (.a(a__inferior), .b(b__inferior), .out(inferior));  // open: cin, cout
  Adder #(.width(32)) adder_1 (
    .a(inferior_t), .b({inferior_1, {16{1'b0}}}), .out(adder_1_out), .cout(adder_1_cout));  // open: cin
  Adder #(.width(32)) adder_2 (.a(superior_1), .b(superior_2), .out(adder_2_out), .cin(adder_1_cout));  // open: cout
  Adder #(.width(32)) adder_3 (
    .a(adder_1_out), .b({inferior_2, {16{1'b0}}}), .out(Outp__Low), .cout(adder_3_cout));  // open: cin
  Adder #(.width(32)) adder_4 (.a(adder_2_out), .b(superior), .out(Outp__High), .cin(adder_3_cout));  // open: cout

  // Other names for the same wires on the sheet: res_inferior[31:0] = Outp__Low; res_superior[31:0] = Outp__High

  // Notes on the sheet:
  //   Resultados:
  //   A dividido en sup. e inf. extendidos cada uno a 32 bits
  //   Formula: A*B = (a*2^k + n) * (b*2^k + m) = a*b*2^[2k] + m*a*2^k + n*b*2^k + n*m 
  //   Distributiva y queda la suma de 4 multiplicaciones. Luego para resolver el signo:
  //   Los bits que se extienden son de 16 a 32 bits, rellenando los bits de 16 a 31 con 0.
  //   a*2^k son los bits superiores de A, b*2^k son los bits superiores de b, n los bits inferiores de A y m los bits inferiores de B.
  //   En complemento A2 si el ultimo bit es 1 ese num tiene signo negativo, por eso se rellenan desde el 16 hasta el ultimo 31 con 0.
  //   De esa forma a, b superiores y a, b inferiores son positivos y se pueden multiplicar usando el mult.
  //   m* a*2^k
  //   n * b*2^k
  //   B dividido en sup. e inf. extendidos cada uno a 32 bits
  //   a*b*2^(2k)
  //   n*m
  //   a*b*2^(2k) + m*a*2^k + n*b*2^k + n*m  
endmodule

module Signed_Div (
  input  [31:0] in_1,
  input  [31:0] in_2,
  output [31:0] Output_L,
  output [31:0] Output_H
);

  wire Signo_Resultante;
  wire [31:0] A_positivo, B_positivo, divider_1_out, divider_1_rem;

  Controlar_Comp__A2 controlar_comp_a2_1 (.num(in_1), .Control(in_1[31]), .Output(A_positivo));
  Controlar_Comp__A2 controlar_comp_a2_2 (.num(in_2), .Control(in_2[31]), .Output(B_positivo));
  Divider #(.width(32)) divider_1 (
    .a(A_positivo), .b(B_positivo), .out(divider_1_out), .rem(divider_1_rem));  // open: upper
  xor xor_1 (Signo_Resultante, in_1[31], in_2[31]);
  Controlar_Comp__A2 controlar_comp_a2_3 (.num(divider_1_out), .Control(Signo_Resultante), .Output(Output_L));
  Controlar_Comp__A2 controlar_comp_a2_4 (.num(divider_1_rem), .Control(Signo_Resultante), .Output(Output_H));

  // Other names for the same wires on the sheet: Signo_Original_A = in_1[31]; Signo_Original_B = in_2[31]

  // Notes on the sheet:
  //   Si el bit 31 es 1 entonces es negativo y se le pasa ese bit como controlador.
  //   Esto es para el signo resultante
  //   Aqui segun el signo resultante se le cambia el signo o no.
endmodule

module Controlar_Comp__A2 (
  input  [31:0] num,
  input  Control,
  output [31:0] Output
);

  wire not_1_out;
  wire [31:0] controlled_buffer_1_out;

  not not_1 (not_1_out, Control);
  assign controlled_buffer_1_out = not_1_out ? num : 32'bz;  // Controlled_Buffer controlled_buffer_1
  assign controlled_buffer_1_out = Control ? ~num : 32'bz;  // Controlled_Inverter controlled_inverter_1
  Adder #(.width(32)) adder_1 (.a(controlled_buffer_1_out), .b({32{1'b0}}), .out(Output), .cin(Control));  // open: cout
endmodule
